# Fritzing sketch Prototype 3.1a (saved by Fritzing 0.8.7b)
breadboards: 1

parts:
  Part1 = Arduino Uno (Rev3)
  R1 = Resistor [tolerance=±5% resistance=220 package=THT]
  LED1 = LED - 5mm [color="Red (633nm)" package="5 mm [THT]"]
  R2 = Resistor [tolerance=±5% resistance=220 package=THT]
  S1 = Pushbutton [package="[THT]"]
  R3 = Resistor [tolerance=±5% resistance=220 package=THT]
  R4 = Resistor [tolerance=±5% resistance=220 package=THT]
  LCD1 = LCD screen
  R5 = Rotary Potentiometer (Small) [maximum_resistance=100kΩ package=THT]
  U1 = Optocoupler [package=THT]
  R6 = Resistor [tolerance=±5% resistance=220 package=THT]

nets:
  N1: Part1.D8, LCD1.RS
  N2: Part1.D10_PWM/SS, LED1.anode
  N3: Part1.D11_PWM/MOSI, R4.Pin_0
  N4: Part1.D12/MISO, R3.Pin_0
  N5: Part1.D13/SCK, R1.Pin_1, S1.Pin_3, S1.Pin_4
  N6: Part1.D2, U1.Pin_5
  N7: Part1.D3_PWM, LCD1.DB7
  N8: Part1.D4, LCD1.DB6
  N9: Part1.D5_PWM, LCD1.DB5
  N10: Part1.D6_PWM, LCD1.DB4
  N11: Part1.D7, LCD1.E
  5V: Part1.5V, S1.Pin_1, S1.Pin_2, LCD1.VDD, R5.leg1
  GND: Part1.GND, R1.Pin_0, R2.Pin_0, LCD1.VSS, LCD1.R/W, R5.leg2, U1.Pin_4
  N12: LED1.cathode, R2.Pin_1
  N13: LCD1.V0, R5.wiper
  N14: U1.Pin_1, R6.Pin_1
